# Fritzing sketch decoder (saved by Fritzing 0.9.2b)

parts:
  Uno32 = chipKIT Motor Shield [package="Motor Shield"]
  LED1 = LED - 5mm [color="Red (633nm)" package="5 mm [THT]"]
  U1 = atmega328 [package=dip]
  R1 = Resistor [tolerance=±5% resistance=470 package=THT]  # not connected
  Patriot_Headphone_Jack_-_Jumper_inside_Patriot = Audio Jack (TRS) 3.5mm [package="PG203J [THT]"]

nets:
  N1: Uno32.5V0, U1.VCC
  N2: Uno32.D35, U1.D3_(PWM)
  N3: Uno32.D39, U1.D1_(TX)
  N4: Uno32.D40, U1.D0_(RX)
  N5: LED1.cathode, U1.GND
  N6: U1.A2, Patriot_Headphone_Jack_-_Jumper_inside_Patriot.Ring
